// Logisim project s5372043_Gaurav_Sood_Logic_Circuit.circ as structural Verilog: 6 circuits, main circuit main
module main (
  input  M1,
  input  M2,
  input  M3,
  input  M4,
  output sign_bit,
  output Stock1,
  output Stock2,
  output Stock4,
  output Stock8,
  output CarryOut
);

  wire ClickToUpdateStockValue_out, n4_bit_full_adder_1_sum1, n4_bit_full_adder_1_sum2,
       n4_bit_full_adder_1_sum3, n4_bit_full_adder_1_sum4, or_1_out, or_2_out, or_3_out, part_a_1_out_5,
       part_a_1_out_6, part_a_1_out_7, part_a_1_out_8, part_a_1_out_9, xor_1_out, xor_2_out;

  Part_A part_a_1 (
    .M1(M1), .M2(M2), .M3(M3), .M4(M4), .out_5(part_a_1_out_5), .out_6(part_a_1_out_6),
    .out_7(part_a_1_out_7), .out_8(part_a_1_out_8), .out_9(part_a_1_out_9));
  or or_1 (or_1_out, part_a_1_out_5, part_a_1_out_8);
  or or_2 (or_2_out, part_a_1_out_8, or_3_out);
  or or_3 (or_3_out, part_a_1_out_6, part_a_1_out_7);
  xor xor_1 (xor_1_out, sign_bit, or_2_out);
  xor xor_2 (xor_2_out, sign_bit, or_1_out);
  or or_4 (sign_bit, part_a_1_out_8, part_a_1_out_7);
  _4_bit_Full_adder u_4_bit_full_adder_1 (
    .A1(xor_1_out), .B1(Stock1), .A2(xor_2_out), .B2(Stock2), .A3(sign_bit), .B3(Stock4), .A4(sign_bit),
    .B4(Stock8), .Sum1(n4_bit_full_adder_1_sum1), .Sum2(n4_bit_full_adder_1_sum2),
    .Sum3(n4_bit_full_adder_1_sum3), .Sum4(n4_bit_full_adder_1_sum4), .Carryin(sign_bit), .Carryout(CarryOut));
  Button ClickToUpdateStockValue (.out(ClickToUpdateStockValue_out));
  D_Flip_Flop d_ff_1 (
    .clk(ClickToUpdateStockValue_out), .D(n4_bit_full_adder_1_sum1), .Q(Stock1));  // open: Qn, preset, en, reset
  D_Flip_Flop d_ff_2 (
    .clk(ClickToUpdateStockValue_out), .D(n4_bit_full_adder_1_sum2), .Q(Stock2));  // open: Qn, preset, en, reset
  D_Flip_Flop d_ff_3 (
    .clk(ClickToUpdateStockValue_out), .D(n4_bit_full_adder_1_sum3), .Q(Stock4));  // open: Qn, preset, en, reset
  D_Flip_Flop d_ff_4 (
    .clk(ClickToUpdateStockValue_out), .D(n4_bit_full_adder_1_sum4), .Q(Stock8));  // open: Qn, preset, en, reset
  LED Month_Error (.in(part_a_1_out_9));

  // Notes on the sheet:
  //   Gaurav Sood, s5372043
  //   Part A & Part B
endmodule

module _4_16decoder (
  input  M1,
  input  M2,
  input  M3,
  input  M4,
  output M0,
  output M1_2,
  output M2_2,
  output M3_2,
  output M4_2,
  output M5,
  output M6,
  output M7,
  output M8,
  output M9,
  output M10,
  output M11,
  output M12,
  output M14,
  output M13,
  output M15
);

  wire and_1_out, and_2_out, and_3_out, and_4_out, and_5_out, and_6_out, and_7_out, and_8_out, and_9_out,
       and_10_out, and_11_out, and_12_out, not_1_out, not_2_out, not_3_out, not_4_out;

  not not_1 (not_1_out, M1);
  not not_2 (not_2_out, M2);
  and and_1 (and_1_out, not_1_out, not_2_out);
  and and_2 (and_2_out, not_1_out, M2);
  and and_3 (and_3_out, M1, not_2_out);
  and and_4 (and_4_out, M1, M2);
  not not_3 (not_3_out, M3);
  and and_5 (and_5_out, and_1_out, not_3_out);
  and and_6 (and_6_out, and_1_out, M3);
  and and_7 (and_7_out, and_2_out, not_3_out);
  and and_8 (and_8_out, and_2_out, M3);
  and and_9 (and_9_out, and_3_out, not_3_out);
  and and_10 (and_10_out, and_3_out, M3);
  and and_11 (and_11_out, and_4_out, not_3_out);
  and and_12 (and_12_out, and_4_out, M3);
  not not_4 (not_4_out, M4);
  and and_13 (M0, and_5_out, not_4_out);
  and and_14 (M1_2, M4, and_5_out);
  and and_15 (M2_2, and_6_out, not_4_out);
  and and_16 (M3_2, and_6_out, M4);
  and and_17 (M4_2, and_7_out, not_4_out);
  and and_18 (M5, and_7_out, M4);
  and and_19 (M6, and_8_out, not_4_out);
  and and_20 (M7, M4, M4, and_8_out);
  and and_21 (M8, and_9_out, not_4_out);
  and and_22 (M9, M4, and_9_out);
  and and_23 (M10, and_10_out, and_10_out, not_4_out);
  and and_24 (M11, M4, and_10_out);
  and and_25 (M12, and_11_out, not_4_out);
  and and_26 (M13, M4, and_11_out);
  and and_27 (M14, and_12_out, not_4_out);
  and and_28 (M15, and_12_out, M4);

  // Notes on the sheet:
  //   2-4 decoder
  //   Gaurav Sood, s5372043
  //   3-8 decoder
  //   4-16 decoder
endmodule

module MonthLogic (
  input  M1_nM2_nM3_nM4,
  input  M1_nM2_nM3M4,
  input  M1_nM2M3_nM4,
  input  M1_nM2M3M4,
  input  M1M2_nM3_nM4,
  input  M1M2_nM3M4,
  input  M1_nM2_nM3_nM4_2,
  input  M1_nM2_nM3M4_2,
  input  M1_nM2M3_nM4_2,
  input  M1_nM2M3M4_2,
  input  M1M2_nM3_nM4_2,
  input  M1M2_nM3M4_2,
  input  M1M2M3_nM4,
  input  M1M2M3_nM4_2,
  input  M1M2M3M4,
  input  M1M2M3M4_2,
  output January,
  output Even_month,
  output Odd_month,
  output December,
  output Error
);

  wire or_1_out, or_2_out, or_3_out, or_4_out, or_5_out, or_6_out, or_8_out, or_9_out;

  or or_1 (or_1_out, M1_nM2_nM3M4, M1_nM2M3_nM4);
  or or_2 (or_2_out, M1_nM2M3M4, M1M2_nM3_nM4);
  or or_3 (or_3_out, M1_nM2_nM3_nM4_2, M1_nM2_nM3M4_2);
  or or_4 (or_4_out, M1_nM2M3_nM4_2, M1_nM2M3M4_2);
  or or_5 (or_5_out, M1M2M3_nM4, M1M2M3_nM4_2);
  or or_6 (or_6_out, M1M2M3M4, M1M2M3M4_2);
  or or_7 (Error, or_5_out, or_6_out);
  or or_8 (or_8_out, or_1_out, or_2_out);
  or or_9 (or_9_out, or_3_out, or_4_out);
  or or_10 (Even_month, or_8_out, M1M2_nM3M4);
  or or_11 (Odd_month, or_9_out, M1M2_nM3_nM4_2);

  assign December = M1M2_nM3M4_2;
  assign January = M1_nM2_nM3_nM4;

  // Notes on the sheet:
  //   Gaurav Sood, s5372043
  //   Month Logic
endmodule

module Part_A (
  input  M1,
  input  M2,
  input  M3,
  input  M4,
  output out_5,
  output out_6,
  output out_7,
  output out_8,
  output out_9
);

  wire n4_16decoder_1_m0, n4_16decoder_1_m1_2, n4_16decoder_1_m2_2, n4_16decoder_1_m3_2, n4_16decoder_1_m4_2,
       n4_16decoder_1_m5, n4_16decoder_1_m6, n4_16decoder_1_m7, n4_16decoder_1_m8, n4_16decoder_1_m9,
       n4_16decoder_1_m10, n4_16decoder_1_m11, n4_16decoder_1_m12, n4_16decoder_1_m13, n4_16decoder_1_m14,
       n4_16decoder_1_m15;

  _4_16decoder u_4_16decoder_1 (
    .M1(M1), .M2(M2), .M3(M3), .M4(M4), .M0(n4_16decoder_1_m0), .M1_2(n4_16decoder_1_m1_2),
    .M2_2(n4_16decoder_1_m2_2), .M3_2(n4_16decoder_1_m3_2), .M4_2(n4_16decoder_1_m4_2),
    .M5(n4_16decoder_1_m5), .M6(n4_16decoder_1_m6), .M7(n4_16decoder_1_m7), .M8(n4_16decoder_1_m8),
    .M9(n4_16decoder_1_m9), .M10(n4_16decoder_1_m10), .M11(n4_16decoder_1_m11), .M12(n4_16decoder_1_m12),
    .M13(n4_16decoder_1_m13), .M14(n4_16decoder_1_m14), .M15(n4_16decoder_1_m15));
  MonthLogic monthlogic_1 (
    .M1_nM2_nM3_nM4(n4_16decoder_1_m0), .M1_nM2_nM3M4(n4_16decoder_1_m2_2),
    .M1_nM2M3_nM4(n4_16decoder_1_m4_2), .M1_nM2M3M4(n4_16decoder_1_m6), .M1M2_nM3_nM4(n4_16decoder_1_m8),
    .M1M2_nM3M4(n4_16decoder_1_m10), .M1_nM2_nM3_nM4_2(n4_16decoder_1_m1_2),
    .M1_nM2_nM3M4_2(n4_16decoder_1_m3_2), .M1_nM2M3_nM4_2(n4_16decoder_1_m5),
    .M1_nM2M3M4_2(n4_16decoder_1_m7), .M1M2_nM3_nM4_2(n4_16decoder_1_m9), .M1M2_nM3M4_2(n4_16decoder_1_m11),
    .M1M2M3_nM4(n4_16decoder_1_m12), .M1M2M3_nM4_2(n4_16decoder_1_m13), .M1M2M3M4(n4_16decoder_1_m14),
    .M1M2M3M4_2(n4_16decoder_1_m15), .January(out_5), .Even_month(out_6), .Odd_month(out_7),
    .December(out_8), .Error(out_9));

  // Notes on the sheet:
  //   Gaurav Sood, s5372043
  //   Part A
endmodule

module Full_Adder (
  input  A1,
  input  B1,
  input  Carry_In,
  output Sum,
  output Carry_out
);

  wire and_1_out, and_2_out, xor_1_out;

  xor xor_1 (xor_1_out, A1, B1);
  and and_1 (and_1_out, A1, B1);
  and and_2 (and_2_out, xor_1_out, Carry_In);
  xor xor_2 (Sum, xor_1_out, Carry_In);
  or or_1 (Carry_out, and_2_out, and_1_out);

  // Notes on the sheet:
  //   Gaurav Sood, s5372043
  //   Full Adder
endmodule

module _4_bit_Full_adder (
  input  Carryin,
  input  A1,
  input  B1,
  input  A2,
  input  B2,
  input  A3,
  input  B3,
  input  A4,
  input  B4,
  output Sum1,
  output Sum2,
  output Sum3,
  output Sum4,
  output Carryout
);

  wire full_adder_1_carry_out, full_adder_2_carry_out, full_adder_3_carry_out;

  Full_Adder full_adder_1 (.A1(Carryin), .B1(A1), .Carry_In(B1), .Sum(Sum1), .Carry_out(full_adder_1_carry_out));
  Full_Adder full_adder_2 (
    .A1(full_adder_1_carry_out), .B1(A2), .Carry_In(B2), .Sum(Sum2), .Carry_out(full_adder_2_carry_out));
  Full_Adder full_adder_3 (
    .A1(full_adder_2_carry_out), .B1(A3), .Carry_In(B3), .Sum(Sum3), .Carry_out(full_adder_3_carry_out));
  Full_Adder full_adder_4 (.A1(full_adder_3_carry_out), .B1(A4), .Carry_In(B4), .Sum(Sum4), .Carry_out(Carryout));

  // Notes on the sheet:
  //   Gaurav Sood, s5372043
  //   4-bit Full Adder
endmodule
